# Fritzing sketch BadUSB Demo.gzz (saved by Fritzing 0.9.3b)
breadboards: 1

parts:
  BadUSB_Demo = Pro Micro
  S2 = Pushbutton [package="[THT]"]
  S3 = Pushbutton [package="[THT]"]

nets:
  N1: BadUSB_Demo.GND, S2.Pin_1, S2.Pin_2, S3.Pin_1, S3.Pin_2
  N2: BadUSB_Demo.D2, S2.Pin_3, S2.Pin_4
  N3: BadUSB_Demo.D3, S3.Pin_3, S3.Pin_4

custom parts:
  Pro Micro: The SparkFun Pro Micro is a complete USB-based microcontoller development system, in a very small footprint, capable of implementing many types of projects. All programming can be done via the USB port.
